// Logisim project 06.circ as structural Verilog: 5 circuits, main circuit JKFF
module JKFF (
  input  J,
  input  K,
  input  Ck,
  output Q,
  output Q_prime
);

  wire and_1_out, and_2_out, and_3_out, and_4_out, nand_1_out, nand_2_out, nor_1_out, nor_2_out, not_1_out;

  not not_1 (not_1_out, Ck);
  nand nand_1 (nand_1_out, J, Q_prime);
  nand nand_2 (nand_2_out, Q, K);
  and and_1 (and_1_out, nand_2_out, J, not_1_out);
  and and_2 (and_2_out, not_1_out, K, nand_1_out);
  nor nor_1 (nor_1_out, and_1_out, nor_2_out);
  nor nor_2 (nor_2_out, nor_1_out, and_2_out);
  and and_3 (and_3_out, nor_1_out, Ck);
  and and_4 (and_4_out, Ck, nor_2_out);
  nor nor_3 (Q, and_3_out, Q_prime);
  nor nor_4 (Q_prime, Q, and_4_out);
endmodule

module _4bit_Counter (
  output [3:0] out_1
);

  wire and_1_out, and_2_out, clock_1_out;

  Clock clock_1 (.out(clock_1_out));
  and and_1 (and_1_out, out_1[2], and_2_out);
  T_Flip_Flop t_ff_1 (.clk(clock_1_out), .T(and_1_out), .Q(out_1[3]), .en(1'b1));  // open: Qn, preset, reset
  and and_2 (and_2_out, out_1[0], out_1[1]);
  T_Flip_Flop t_ff_2 (.clk(clock_1_out), .T(and_2_out), .Q(out_1[2]), .en(1'b1));  // open: Qn, preset, reset
  T_Flip_Flop t_ff_3 (.clk(clock_1_out), .T(out_1[0]), .Q(out_1[1]), .en(1'b1));  // open: Qn, preset, reset
  T_Flip_Flop t_ff_4 (.clk(clock_1_out), .T(1'b1), .Q(out_1[0]), .en(1'b1));  // open: Qn, preset, reset
endmodule

module _3x8 (
  input  C2,
  input  C1,
  input  C0,
  input  E,
  output D0,
  output D1,
  output D2,
  output D3,
  output D4,
  output D5,
  output D6,
  output D7
);

  wire not_1_out, not_2_out, not_3_out;

  not not_1 (not_1_out, C2);
  not not_2 (not_2_out, C1);
  not not_3 (not_3_out, C0);
  and and_1 (D0, not_1_out, not_2_out, not_3_out, E);
  and and_2 (D1, not_1_out, not_2_out, C0, E);
  and and_3 (D2, not_1_out, C1, not_3_out, E);
  and and_4 (D3, not_1_out, C1, C0, E);
  and and_5 (D4, C2, not_2_out, not_3_out, E);
  and and_6 (D5, C2, not_2_out, C0, E);
  and and_7 (D6, C2, C1, not_3_out);
  and and_8 (D7, C2, C1, C0, E);
endmodule

module _3x8dec__1x8deMux (
  input  in_1,
  input  [2:0] in_2,
  input  in_3,
  input  [2:0] in_4,
  output out_5,
  output out_6,
  output out_7,
  output out_8,
  output out_9,
  output out_10,
  output out_11,
  output out_12,
  output out_13,
  output out_14,
  output out_15,
  output out_16,
  output out_17,
  output out_18,
  output out_19,
  output out_20
);

  Multiplexer #(.select(3)) multiplexer_1 (
    .in0(out_5), .in1(out_6), .in2(out_7), .in3(out_8), .in4(out_9), .in5(out_10), .in6(out_11),
    .in7(out_12), .sel(in_2), .en(in_1));  // open: out
  Decoder #(.select(3)) decoder_1 (
    .out0(out_13), .out1(out_14), .out2(out_15), .out3(out_16), .out4(out_17), .out5(out_18), .out6(out_19),
    .out7(out_20), .sel(in_4), .en(in_3));
endmodule

module _4x16_dec (
  input  in_1,
  input  in_2,
  input  in_3,
  input  in_4,
  output out_5,
  output out_6,
  output out_7,
  output out_8,
  output out_9,
  output out_10,
  output out_11,
  output out_12,
  output out_13,
  output out_14,
  output out_15,
  output out_16,
  output out_17,
  output out_18,
  output out_19,
  output out_20
);

  wire not_1_out;

  not not_1 (not_1_out, in_1);
  _3x8 u_3x8_1 (
    .C2(in_2), .C1(in_3), .C0(in_4), .E(not_1_out), .D0(out_5), .D1(out_6), .D2(out_7), .D3(out_8),
    .D4(out_9), .D5(out_10), .D6(out_11), .D7(out_12));
  _3x8 u_3x8_2 (
    .C2(in_2), .C1(in_3), .C0(in_4), .E(in_1), .D0(out_13), .D1(out_14), .D2(out_15), .D3(out_16),
    .D4(out_17), .D5(out_18), .D6(out_19), .D7(out_20));
endmodule
