// Logisim project 07.circ as structural Verilog: 1 circuit, main circuit main
module main (
);

  Multiplexer multiplexer_1 ();  // open: in0, in1, out, sel, en
  Register AC ();  // open: D, en, Q, clk, clr
  Register PC ();  // open: D, en, Q, clk, clr
  Register IR_Addr ();  // open: D, en, Q, clk, clr
  Register MBR ();  // open: D, en, Q, clk, clr
  Register MAR ();  // open: D, en, Q, clk, clr
endmodule
