// Logisim project 08_CU구현.circ as structural Verilog: 14 circuits, main circuit 2x1 MUX
// 2x1 mux
module _2x1_MUX (
  input  s,
  input  i0,
  input  i1,
  output out_4
);

  wire and_1_out, and_2_out, not_1_out;

  not not_1 (not_1_out, s);
  and and_1 (and_1_out, not_1_out, i0);
  and and_2 (and_2_out, s, i1);
  or or_1 (out_4, and_1_out, and_2_out);
endmodule

module _4x1MUX (
  input  in_1,
  input  in_2,
  input  in_3,
  input  in_4,
  input  in_5,
  input  in_6,
  output out_7
);

  wire and_1_out, and_2_out, and_3_out, and_4_out, not_1_out, not_2_out;

  not not_1 (not_1_out, in_1);
  not not_2 (not_2_out, in_2);
  and and_1 (and_1_out, not_2_out, not_1_out, in_3);
  and and_2 (and_2_out, in_2, not_1_out, in_4);
  and and_3 (and_3_out, not_2_out, in_1, in_5);
  and and_4 (and_4_out, in_2, in_1, in_6);
  or or_1 (out_7, and_1_out, and_2_out, and_3_out, and_4_out);
endmodule

// 1LU
module _1bit_LU (
  input  in_1,
  input  in_2,
  input  in_3,
  input  in_4,
  output out_5
);

  wire and_1_out, not_1_out, or_1_out, xor_1_out;

  and and_1 (and_1_out, in_1, in_2);
  or or_1 (or_1_out, in_1, in_2);
  xor xor_1 (xor_1_out, in_1, in_2);
  not not_1 (not_1_out, in_1);
  _4x1MUX u_4x1mux_1 (
    .in_1(in_3), .in_2(in_4), .in_3(and_1_out), .in_4(or_1_out), .in_5(xor_1_out), .in_6(not_1_out),
    .out_7(out_5));
endmodule

module _4bit_LU (
  input  [3:0] i0,
  input  [3:0] i1,
  input  s1,
  input  s0,
  output [3:0] o
);

  _1bit_LU u_1bit_lu_1 (.in_1(i0[0]), .in_2(i1[0]), .in_3(s1), .in_4(s0), .out_5(o[0]));
  _1bit_LU u_1bit_lu_2 (.in_1(i0[1]), .in_2(i1[1]), .in_3(s1), .in_4(s0), .out_5(o[1]));
  _1bit_LU u_1bit_lu_3 (.in_1(i0[2]), .in_2(i1[2]), .in_3(s1), .in_4(s0), .out_5(o[2]));
  _1bit_LU u_1bit_lu_4 (.in_1(i0[3]), .in_2(i1[3]), .in_3(s1), .in_4(s0), .out_5(o[3]));
endmodule

// 4bit Shift
module _4bit_shifter (
  input  SLin,
  input  [3:0] Input,
  input  SRin,
  input  SR,
  input  SL,
  output SRo,
  output [3:0] O,
  output SLo
);

  and and_1 (SRo, Input[0], SR);
  _4x1MUX u_4x1mux_1 (.in_1(SR), .in_2(SL), .in_3(Input[0]), .in_4(SLin), .in_5(Input[1]), .out_7(O[0]));  // open: in_6
  _4x1MUX u_4x1mux_2 (
    .in_1(SR), .in_2(SL), .in_3(Input[1]), .in_4(Input[0]), .in_5(Input[2]), .out_7(O[1]));  // open: in_6
  _4x1MUX u_4x1mux_3 (
    .in_1(SR), .in_2(SL), .in_3(Input[2]), .in_4(Input[1]), .in_5(Input[3]), .out_7(O[2]));  // open: in_6
  _4x1MUX u_4x1mux_4 (.in_1(SR), .in_2(SL), .in_3(Input[3]), .in_4(Input[2]), .in_5(SRin), .out_7(O[3]));  // open: in_6
  and and_2 (SLo, SL, Input[3]);
endmodule

// 8SH
module _8bit_shifter (
  input  in_1,
  input  [7:0] I,
  input  SR,
  input  SL,
  input  in_5,
  output [7:0] O
);

  wire n4bit_shifter_1_slo, n4bit_shifter_2_sro;

  _4bit_shifter u_4bit_shifter_1 (
    .SLin(in_1), .Input(I[3:0]), .SRin(n4bit_shifter_2_sro), .SR(SR), .SL(SL), .O(O[3:0]),
    .SLo(n4bit_shifter_1_slo));  // open: SRo
  _4bit_shifter u_4bit_shifter_2 (
    .SLin(n4bit_shifter_1_slo), .Input(I[7:4]), .SRin(in_5), .SR(SR), .SL(SL), .SRo(n4bit_shifter_2_sro),
    .O(O[7:4]));  // open: SLo
endmodule

// 8LU
module _8bit_LU (
  input  [7:0] in_1,
  input  [7:0] in_2,
  input  s1,
  input  s0,
  output [7:0] out_5
);

  _4bit_LU u_4bit_lu_1 (.i0(in_1[3:0]), .i1(in_2[3:0]), .s1(s1), .s0(s0), .o(out_5[3:0]));
  _4bit_LU u_4bit_lu_2 (.i0(in_1[7:4]), .i1(in_2[7:4]), .s1(s1), .s0(s0), .o(out_5[7:4]));
endmodule

// 1AU
module _1bit_AU (
  input  ci,
  input  A,
  input  B,
  input  s1,
  input  s0,
  output s,
  output co
);

  wire n4x1mux_1_out_7, not_1_out;

  not not_1 (not_1_out, B);
  _4x1MUX u_4x1mux_1 (
    .in_1(s1), .in_2(s0), .in_3(1'b0), .in_4(B), .in_5(not_1_out), .in_6(1'b1), .out_7(n4x1mux_1_out_7));
  full_adder full_adder_1 (.a(ci), .b(A), .ci(n4x1mux_1_out_7), .s(s), .co(co));
endmodule

// FA
module full_adder (
  input  a,
  input  b,
  input  ci,
  output s,
  output co
);

  wire and_1_out, and_2_out, and_3_out, and_4_out, and_5_out, and_6_out, and_7_out, not_1_out, not_2_out,
       not_3_out, not_4_out, not_5_out, not_6_out;

  not not_1 (not_1_out, a);
  not not_2 (not_2_out, b);
  not not_3 (not_3_out, a);
  not not_4 (not_4_out, ci);
  not not_5 (not_5_out, b);
  not not_6 (not_6_out, ci);
  and and_1 (and_1_out, b, ci);
  and and_2 (and_2_out, a, ci);
  and and_3 (and_3_out, a, b);
  and and_4 (and_4_out, not_1_out, not_2_out, ci);
  and and_5 (and_5_out, not_3_out, b, not_4_out);
  and and_6 (and_6_out, a, not_5_out, not_6_out);
  and and_7 (and_7_out, a, b, ci);
  or or_1 (co, and_1_out, and_2_out, and_3_out);
  or or_2 (s, and_4_out, and_5_out, and_6_out, and_7_out);
endmodule

// 8AU
module _8bit_AU (
  input  ci,
  input  [7:0] i0,
  input  [7:0] i1,
  input  s1,
  input  s0,
  output [7:0] o,
  output v,
  output co
);

  wire n1bit_au_1_co, n1bit_au_2_co, n1bit_au_3_co, n1bit_au_4_co, n1bit_au_5_co, n1bit_au_6_co,
       n1bit_au_7_co;

  _1bit_AU u_1bit_au_1 (.ci(ci), .A(i0[0]), .B(i1[0]), .s1(s1), .s0(s0), .s(o[0]), .co(n1bit_au_1_co));
  _1bit_AU u_1bit_au_2 (.ci(n1bit_au_1_co), .A(i0[1]), .B(i1[1]), .s1(s1), .s0(s0), .s(o[1]), .co(n1bit_au_2_co));
  _1bit_AU u_1bit_au_3 (.ci(n1bit_au_2_co), .A(i0[2]), .B(i1[2]), .s1(s1), .s0(s0), .s(o[2]), .co(n1bit_au_3_co));
  _1bit_AU u_1bit_au_4 (.ci(n1bit_au_3_co), .A(i0[3]), .B(i1[3]), .s1(s1), .s0(s0), .s(o[3]), .co(n1bit_au_4_co));
  _1bit_AU u_1bit_au_5 (.ci(n1bit_au_4_co), .A(i0[4]), .B(i1[4]), .s1(s1), .s0(s0), .s(o[4]), .co(n1bit_au_5_co));
  _1bit_AU u_1bit_au_6 (.ci(n1bit_au_5_co), .A(i0[5]), .B(i1[5]), .s1(s1), .s0(s0), .s(o[5]), .co(n1bit_au_6_co));
  _1bit_AU u_1bit_au_7 (.ci(n1bit_au_6_co), .A(i0[6]), .B(i1[6]), .s1(s1), .s0(s0), .s(o[6]), .co(n1bit_au_7_co));
  _1bit_AU u_1bit_au_8 (.ci(n1bit_au_7_co), .A(i0[7]), .B(i1[7]), .s1(s1), .s0(s0), .s(o[7]), .co(co));
  xor xor_1 (v, n1bit_au_7_co, co);
endmodule

// 8 2x1
module _8bit_2X1_mux (
  input  [7:0] a,
  input  [7:0] b,
  input  s,
  output [7:0] out_4
);

  _2x1_MUX u_2x1_mux_1 (.s(s), .i0(a[0]), .i1(b[0]), .out_4(out_4[0]));
  _2x1_MUX u_2x1_mux_2 (.s(s), .i0(a[1]), .i1(b[1]), .out_4(out_4[1]));
  _2x1_MUX u_2x1_mux_3 (.s(s), .i0(a[2]), .i1(b[2]), .out_4(out_4[2]));
  _2x1_MUX u_2x1_mux_4 (.s(s), .i0(a[3]), .i1(b[3]), .out_4(out_4[3]));
  _2x1_MUX u_2x1_mux_5 (.s(s), .i0(a[4]), .i1(b[4]), .out_4(out_4[4]));
  _2x1_MUX u_2x1_mux_6 (.s(s), .i0(a[5]), .i1(b[5]), .out_4(out_4[5]));
  _2x1_MUX u_2x1_mux_7 (.s(s), .i0(a[6]), .i1(b[6]), .out_4(out_4[6]));
  _2x1_MUX u_2x1_mux_8 (.s(s), .i0(a[7]), .i1(b[7]), .out_4(out_4[7]));
endmodule

module _8bit_ALU (
  input  [7:0] A,
  input  [7:0] B,
  input  [3:0] in_3,
  output v,
  output c,
  output z,
  output [7:0] out_7,
  output s
);

  wire [7:0] n8bit_2x1_mux_1_out_4, n8bit_au_1_o, n8bit_lu_1_out_5, n8bit_shifter_1_o;

  _8bit_AU u_8bit_au_1 (.ci(in_3[0]), .i0(A), .i1(B), .s1(in_3[2]), .s0(in_3[1]), .o(n8bit_au_1_o), .co(c), .v(v));
  _8bit_LU u_8bit_lu_1 (.in_1(A), .in_2(B), .s1(in_3[2]), .s0(in_3[1]), .out_5(n8bit_lu_1_out_5));
  _8bit_shifter u_8bit_shifter_1 (.in_1(1'b0), .I(A), .SR(in_3[2]), .SL(in_3[1]), .in_5(1'b0), .O(n8bit_shifter_1_o));
  _8bit_2X1_mux u_8bit_2x1_mux_1 (
    .a(n8bit_lu_1_out_5), .b(n8bit_shifter_1_o), .s(in_3[0]), .out_4(n8bit_2x1_mux_1_out_4));
  _8bit_2X1_mux u_8bit_2x1_mux_2 (.a(n8bit_au_1_o), .b(n8bit_2x1_mux_1_out_4), .s(in_3[3]), .out_4(out_7));
  nor nor_1 (z, out_7[0], out_7[1], out_7[2], out_7[3], out_7[4], out_7[5], out_7[6], out_7[7]);

  assign s = out_7[7];

  // Notes on the sheet:
  //   s2==0 : AU
  //   s2,ci == 1,0 : LU
  //   s2, ci == 1,1, : shift
endmodule

module CU (
  input  Ck,
  input  RST,
  input  [7:0] IR_Op,
  input  [3:0] st,
  output M,
  output [2:0] out_6,
  output [6:0] LDs,
  output [1:0] R,
  output [3:0] ALU,
  output RW
);

  wire AC2BR, ADD, ADD_T4, ADD_T5, ADD_T7, AND, BR2AC, BZ, IRAD2AR, IRAD2PC, JMP, LDA, LDA_T4, LDA_T5,
       LDA_T7, NOP, NOT, not_1_out, OR, or_2_out, READ, SHL, SHR, STR, STR_T4, STR_T6, STR_T7, SUB, T0, T1,
       T4, T5, T6, T7, XOR;

  and and_1 (LDA_T4, LDA, T4);
  and and_2 (LDA_T5, LDA, T5);
  and and_3 (BR2AC, LDA, T6);
  not not_1 (not_1_out, Ck);
  not not_2 (RW, STR_T6);
  or or_1 (IRAD2AR, LDA_T4, ADD_T4, STR_T4);
  Counter #(.width(3), .max('h7)) counter_1 (
    .Q(out_6), .clk(not_1_out), .clr(or_2_out));  // open: load, D, count, carry
  or or_2 (or_2_out, STR_T7, ADD_T7, LDA_T7);
  or or_3 (R[0], T0, T1, LDs[1], LDs[4], BR2AC);
  Decoder #(.select(3), .enable("false")) decoder_1 (
    .out0(T0), .out1(T1), .out2(LDs[1]), .out3(LDs[4]), .out4(T4), .out5(T5), .out6(T6), .out7(T7),
    .sel(out_6));
  Decoder #(.select(4), .enable("false")) decoder_2 (
    .out0(NOP), .out1(NOT), .out2(SHL), .out3(SHR), .out4(JMP), .out5(BZ), .out8(LDA), .out9(ADD),
    .out10(SUB), .out11(AND), .out12(OR), .out13(XOR), .out15(STR), .sel(IR_Op[7:4]));  // open: out6, out7, out14
  or or_4 (R[1], IRAD2AR, IRAD2PC, LDs[4], BR2AC);
  and and_4 (ADD_T4, ADD, T4);
  and and_5 (ADD_T5, ADD, T5);
  and and_6 (ALU[1], ADD, T6);
  and and_7 (STR_T7, STR, T7);
  and and_8 (ADD_T7, ADD, T7);
  and and_9 (LDA_T7, LDA, T7);
  and and_10 (STR_T4, STR, T4);
  and and_11 (AC2BR, STR, T5);
  and and_12 (STR_T6, STR, T6);
  or or_5 (READ, LDA_T5, ADD_T5);
  or or_6 (LDs[3], READ, T1, LDs[1], AC2BR);
  and and_13 (IRAD2PC, JMP, T4);
  or or_7 (M, T1, READ, LDs[1]);
  or or_8 (LDs[2], T1, IRAD2AR, T0);
  or or_9 (LDs[5], T1, IRAD2PC, T0);
  or or_10 (LDs[6], BR2AC, ALU[1]);
  or or_11 (ALU[0], T1, LDs[1]);

  assign ALU[3:2] = 2'b00;
  assign LDs[0] = LDs[6];

  // Other names for the same wires on the sheet: ADD_T6 = ALU[1]; uADD = ALU[1]; JMP_T4 = IRAD2PC; LDA_T6 = BR2AC;
  //   T2 = LDs[1]; T3 = LDs[4]; V = st[0]; C = st[1]; Z = st[2]; S = st[3]; STR_T5 = AC2BR; WRITE = STR_T6
endmodule

module CPU (
  input  in_1,
  input  in_2
);

  wire acld, clock_1_out, iraddld, iropld, M, marld, mbrld, not_1_out, pcld, RW, stld;
  wire [1:0] R;
  wire [2:0] cu_1_out_6;
  wire [3:0] ALU, n8bit_alu_1_v, status_q;
  wire [7:0] AC_q, controlled_buffer_1_out, IR_Addr_q, IR_Op_q, MAR_q, MBR_q, multiplexer_1_out,
       multiplexer_2_out, n8bit_alu_1_out_7, PC_q;

  Multiplexer #(.width(8), .enable("false")) multiplexer_1 (
    .in0(n8bit_alu_1_out_7), .in1(controlled_buffer_1_out), .out(multiplexer_1_out), .sel(M));
  Register AC (.D(n8bit_alu_1_out_7), .en(acld), .Q(AC_q), .clk(clock_1_out), .clr(in_1));
  Register PC (.D(n8bit_alu_1_out_7), .en(pcld), .Q(PC_q), .clk(clock_1_out), .clr(in_1));
  Register IR_Addr (.D(n8bit_alu_1_out_7), .en(iraddld), .Q(IR_Addr_q), .clk(clock_1_out), .clr(in_1));
  Register MBR (.D(multiplexer_1_out), .en(mbrld), .Q(MBR_q), .clk(clock_1_out), .clr(in_1));
  Register MAR (.D(n8bit_alu_1_out_7), .en(marld), .Q(MAR_q), .clk(clock_1_out), .clr(in_1));
  Clock clock_1 (.out(clock_1_out));
  assign controlled_buffer_1_out = not_1_out ? MBR_q : 8'bz;  // Controlled_Buffer controlled_buffer_1
  not not_1 (not_1_out, RW);
  Register IR_Op (.D(MBR_q), .en(iropld), .Q(IR_Op_q), .clk(clock_1_out), .clr(in_1));
  Multiplexer #(.select(2), .width(8), .enable("false")) multiplexer_2 (
    .in0(AC_q), .in1(PC_q), .in2(IR_Addr_q), .in3(MBR_q), .out(multiplexer_2_out), .sel(R));
  // Probe on multiplexer_2_out
  // Probe on MBR_q
  Register #(.width(4)) status (.D(n8bit_alu_1_v), .en(stld), .Q(status_q), .clk(clock_1_out), .clr(in_1));
  // Probe on n8bit_alu_1_out_7
  _8bit_ALU u_8bit_alu_1 (
    .A(multiplexer_2_out), .B(MBR_q), .in_3(ALU), .out_7(n8bit_alu_1_out_7), .v(n8bit_alu_1_v[0]),
    .c(n8bit_alu_1_v[1]), .z(n8bit_alu_1_v[2]), .s(n8bit_alu_1_v[3]));
  // Probe on cu_1_out_6
  CU cu_1 (
    .Ck(clock_1_out), .RST(in_1), .st(status_q), .IR_Op(IR_Op_q), .R(R), .M(M), .ALU(ALU),
    .LDs({acld, pcld, iraddld, mbrld, marld, iropld, stld}), .RW(RW), .out_6(cu_1_out_6));
  RAM ram_1 (.addr(MAR_q), .data(controlled_buffer_1_out), .sel(in_2), .clk(clock_1_out), .ld(RW));  // open: clr
endmodule
