// Logisim project CPU.circ as structural Verilog: 2 circuits, main circuit CU
module CU (
  input  Ck,
  input  RST,
  input  [3:0] st,
  input  [7:0] IR_Op,
  output [2:0] cnt,
  output rw,
  output [1:0] R,
  output M,
  output [3:0] ALU,
  output [6:0] LDs
);

  wire not_1_out, T0, T1;

  Counter #(.width(3), .max('h7)) u_Cnt (.Q(cnt), .clk(not_1_out), .clr(RST));  // open: load, D, count, carry
  not not_1 (not_1_out, Ck);
  or or_1 (ALU[0], T1, LDs[1]);
  or or_2 (LDs[2], T0, T1);
  Decoder #(.select(3), .enable("false")) decoder_1 (
    .out0(T0), .out1(T1), .out2(LDs[1]), .out3(LDs[4]), .sel(cnt));  // open: out4, out5, out6, out7

  assign ALU[3:1] = 3'b000;
  assign {LDs[6:5], LDs[3], LDs[0]} = {1'b0, {2{ALU[0]}}, 1'b0};
  assign M = ALU[0];
  assign R = {LDs[4], 1'b1};
  assign rw = 1'b1;

  // Other names for the same wires on the sheet: T2 = LDs[1]; T3 = LDs[4]
endmodule

module CPU (
  input  in_1,
  input  in_2
);

  wire acld, clock_1_out, iraddrld, iropld, M, marld, mbrld, not_1_out, pcld, RW, stld;
  wire [1:0] R;
  wire [3:0] ALU, status_q, undriven_2;
  wire [7:0] AC_q, controlled_buffer_1_out, IR_Addr_q, IR_Op_q, MAR_q, MBR_q, multiplexer_1_out,
       multiplexer_2_out, PC_q, undriven;

  Multiplexer #(.width(8), .enable("false")) multiplexer_1 (
    .in0(undriven), .in1(controlled_buffer_1_out), .out(multiplexer_1_out), .sel(M));
  Clock clock_1 (.out(clock_1_out));
  Register AC (.D(undriven), .en(acld), .Q(AC_q), .clk(clock_1_out), .clr(in_1));
  Register PC (.D(undriven), .en(pcld), .Q(PC_q), .clk(clock_1_out), .clr(in_1));
  Register IR_Addr (.D(undriven), .en(iraddrld), .Q(IR_Addr_q), .clk(clock_1_out), .clr(in_1));
  Register MBR (.D(multiplexer_1_out), .en(mbrld), .Q(MBR_q), .clk(clock_1_out), .clr(in_1));
  Register MAR (.D(undriven), .en(marld), .Q(MAR_q), .clk(clock_1_out), .clr(in_1));
  Multiplexer #(.select(2), .width(8), .enable("false")) multiplexer_2 (
    .in0(AC_q), .in1(PC_q), .in2(IR_Addr_q), .in3(MBR_q), .out(multiplexer_2_out), .sel(R));
  assign controlled_buffer_1_out = not_1_out ? MBR_q : 8'bz;  // Controlled_Buffer controlled_buffer_1
  not not_1 (not_1_out, RW);
  Register #(.width(4)) status (.D(undriven_2), .en(stld), .Q(status_q), .clk(clock_1_out), .clr(in_1));
  Register IR_Op (.D(MBR_q), .en(iropld), .Q(IR_Op_q), .clk(clock_1_out), .clr(in_1));
  CU cu_1 (
    .Ck(clock_1_out), .RST(in_1), .st(status_q), .IR_Op(IR_Op_q), .rw(RW), .R(R), .M(M), .ALU(ALU),
    .LDs({acld, pcld, iraddrld, mbrld, marld, iropld, stld}));  // open: cnt
  RAM ram_1 (.addr(MAR_q), .data(controlled_buffer_1_out), .sel(in_2), .clk(clock_1_out), .ld(RW));  // open: clr
endmodule
