// Logisim project MUX.circ as structural Verilog: 5 circuits, main circuit 2x1 MUX
module _2x1_MUX (
  input  in_1,
  input  in_2,
  input  in_3,
  output out_4
);

  wire and_1_out, and_2_out, not_1_out;

  not not_1 (not_1_out, in_1);
  and and_1 (and_1_out, not_1_out, in_2);
  and and_2 (and_2_out, in_1, in_3);
  or or_1 (out_4, and_1_out, and_2_out);
endmodule

module _4x1MUX (
  input  in_1,
  input  in_2,
  input  in_3,
  input  in_4,
  input  in_5,
  input  in_6,
  output out_7
);

  wire and_1_out, and_2_out, and_3_out, and_4_out, not_1_out, not_2_out;

  not not_1 (not_1_out, in_1);
  not not_2 (not_2_out, in_2);
  and and_1 (and_1_out, not_2_out, not_1_out, in_3);
  and and_2 (and_2_out, in_2, not_1_out, in_4);
  and and_3 (and_3_out, not_2_out, in_1, in_5);
  and and_4 (and_4_out, in_2, in_1, in_6);
  or or_1 (out_7, and_1_out, and_2_out, and_3_out, and_4_out);
endmodule

// 1LU
module _1bit_LU (
  input  in_1,
  input  in_2,
  input  in_3,
  input  in_4,
  output out_5
);

  wire and_1_out, not_1_out, or_1_out, xor_1_out;

  and and_1 (and_1_out, in_1, in_2);
  or or_1 (or_1_out, in_1, in_2);
  xor xor_1 (xor_1_out, in_1, in_2);
  not not_1 (not_1_out, in_1);
  _4x1MUX u_4x1mux_1 (
    .in_1(in_3), .in_2(in_4), .in_3(and_1_out), .in_4(or_1_out), .in_5(xor_1_out), .in_6(not_1_out),
    .out_7(out_5));
endmodule

// 4x1 mux
module _4bit_LU (
  input  [3:0] in_1,
  input  [3:0] in_2,
  input  in_3,
  input  in_4,
  output [3:0] out_5
);

  _1bit_LU u_1bit_lu_1 (.in_1(in_1[0]), .in_2(in_2[0]), .in_3(in_3), .in_4(in_4), .out_5(out_5[0]));
  _1bit_LU u_1bit_lu_2 (.in_1(in_1[1]), .in_2(in_2[1]), .in_3(in_3), .in_4(in_4), .out_5(out_5[1]));
  _1bit_LU u_1bit_lu_3 (.in_1(in_1[2]), .in_2(in_2[2]), .in_3(in_3), .in_4(in_4), .out_5(out_5[2]));
  _1bit_LU u_1bit_lu_4 (.in_1(in_1[3]), .in_2(in_2[3]), .in_3(in_3), .in_4(in_4), .out_5(out_5[3]));
endmodule

module _4bit_shifter (
  input  in_1,
  input  [3:0] in_2,
  input  in_3,
  input  in_4,
  input  in_5,
  output [3:0] out_6
);

  _4x1MUX u_4x1mux_1 (
    .in_1(in_4), .in_2(in_5), .in_3(in_2[0]), .in_4(in_1), .in_5(in_2[1]), .out_7(out_6[0]));  // open: in_6
  _4x1MUX u_4x1mux_2 (
    .in_1(in_4), .in_2(in_5), .in_3(in_2[1]), .in_4(in_2[0]), .in_5(in_2[2]), .out_7(out_6[1]));  // open: in_6
  _4x1MUX u_4x1mux_3 (
    .in_1(in_4), .in_2(in_5), .in_3(in_2[2]), .in_4(in_2[1]), .in_5(in_2[3]), .out_7(out_6[2]));  // open: in_6
  _4x1MUX u_4x1mux_4 (
    .in_1(in_4), .in_2(in_5), .in_3(in_2[3]), .in_4(in_2[2]), .in_5(in_3), .out_7(out_6[3]));  // open: in_6
endmodule
