// Logisim project adder.circ as structural Verilog
module HA (
  input  in_1,
  input  in_2,
  output out_3,
  output out_4
);

  xor xor_1 (out_3, in_1, in_2);
  and and_1 (out_4, in_1, in_2);
endmodule

// FA
module full_adder (
  input  a,
  input  b,
  input  c,
  output s,
  output c_2
);

  wire ha_1_out_3, ha_1_out_4, ha_2_out_4;

  HA ha_1 (.in_1(a), .out_3(ha_1_out_3), .in_2(b), .out_4(ha_1_out_4));
  HA ha_2 (.in_1(ha_1_out_3), .out_3(s), .in_2(c), .out_4(ha_2_out_4));
  or or_1 (c_2, ha_2_out_4, ha_1_out_4);
endmodule

// 4bit-adder
module _4bit_adder (
  input  in_1,
  input  [3:0] in_2,
  input  [3:0] in_3,
  output [3:0] out_4,
  output out_5
);

  wire full_adder_1_c_2, full_adder_2_c_2, full_adder_3_c_2;

  full_adder full_adder_1 (.a(in_2[0]), .b(in_3[0]), .c(in_1), .s(out_4[0]), .c_2(full_adder_1_c_2));
  full_adder full_adder_2 (.a(in_2[1]), .b(in_3[1]), .c(full_adder_1_c_2), .s(out_4[1]), .c_2(full_adder_2_c_2));
  full_adder full_adder_3 (.a(in_2[2]), .b(in_3[2]), .c(full_adder_2_c_2), .s(out_4[2]), .c_2(full_adder_3_c_2));
  full_adder full_adder_4 (.a(in_2[3]), .b(in_3[3]), .c(full_adder_3_c_2), .s(out_4[3]), .c_2(out_5));
endmodule

module _16bit_adder_4bitx4 (
  input  in_1,
  input  [7:0] in_2,
  input  [7:0] in_3,
  input  [7:0] in_4,
  input  [7:0] in_5,
  output [15:0] out_6,
  output out_7
);

  wire n4bit_adder_1_out_5, n4bit_adder_2_out_5, n4bit_adder_3_out_5;

  _4bit_adder u_4bit_adder_1 (
    .in_2(in_2[3:0]), .in_3(in_2[7:4]), .out_4(out_6[3:0]), .in_1(in_1), .out_5(n4bit_adder_1_out_5));
  _4bit_adder u_4bit_adder_2 (
    .in_2(in_3[3:0]), .in_3(in_3[7:4]), .out_4(out_6[7:4]), .in_1(n4bit_adder_1_out_5),
    .out_5(n4bit_adder_2_out_5));
  _4bit_adder u_4bit_adder_3 (
    .in_2(in_4[3:0]), .in_3(in_4[7:4]), .out_4(out_6[11:8]), .in_1(n4bit_adder_2_out_5),
    .out_5(n4bit_adder_3_out_5));
  _4bit_adder u_4bit_adder_4 (
    .in_2(in_5[3:0]), .in_3(in_5[7:4]), .out_4(out_6[15:12]), .in_1(n4bit_adder_3_out_5), .out_5(out_7));
endmodule

module _16bit_adder_FAx16 (
  input  in_1,
  input  [7:0] in_2,
  input  [7:0] in_3,
  input  [7:0] in_4,
  input  [7:0] in_5,
  output [15:0] out_6,
  output out_7
);

  wire full_adder_1_c_2, full_adder_2_c_2, full_adder_3_c_2, full_adder_4_c_2, full_adder_5_c_2,
       full_adder_6_c_2, full_adder_7_c_2, full_adder_8_c_2, full_adder_9_c_2, full_adder_10_c_2,
       full_adder_11_c_2, full_adder_12_c_2, full_adder_13_c_2, full_adder_14_c_2, full_adder_15_c_2;

  full_adder full_adder_1 (.a(in_2[0]), .b(in_2[4]), .c(in_1), .s(out_6[0]), .c_2(full_adder_1_c_2));
  full_adder full_adder_2 (.a(in_2[1]), .b(in_2[5]), .c(full_adder_1_c_2), .s(out_6[1]), .c_2(full_adder_2_c_2));
  full_adder full_adder_3 (.a(in_2[2]), .b(in_2[6]), .c(full_adder_2_c_2), .s(out_6[2]), .c_2(full_adder_3_c_2));
  full_adder full_adder_4 (.a(in_2[3]), .b(in_2[7]), .c(full_adder_3_c_2), .s(out_6[3]), .c_2(full_adder_4_c_2));
  full_adder full_adder_5 (.a(in_4[0]), .b(in_4[4]), .c(full_adder_4_c_2), .s(out_6[4]), .c_2(full_adder_5_c_2));
  full_adder full_adder_6 (.a(in_4[1]), .b(in_4[5]), .c(full_adder_5_c_2), .s(out_6[5]), .c_2(full_adder_6_c_2));
  full_adder full_adder_7 (.a(in_4[2]), .b(in_4[6]), .c(full_adder_6_c_2), .s(out_6[6]), .c_2(full_adder_7_c_2));
  full_adder full_adder_8 (.a(in_4[3]), .b(in_4[7]), .c(full_adder_7_c_2), .s(out_6[7]), .c_2(full_adder_8_c_2));
  full_adder full_adder_9 (.a(in_3[0]), .b(in_3[4]), .c(full_adder_8_c_2), .s(out_6[8]), .c_2(full_adder_9_c_2));
  full_adder full_adder_10 (.a(in_3[1]), .b(in_3[5]), .c(full_adder_9_c_2), .s(out_6[9]), .c_2(full_adder_10_c_2));
  full_adder full_adder_11 (.a(in_3[2]), .b(in_3[6]), .c(full_adder_10_c_2), .s(out_6[10]), .c_2(full_adder_11_c_2));
  full_adder full_adder_12 (.a(in_3[3]), .b(in_3[7]), .c(full_adder_11_c_2), .s(out_6[11]), .c_2(full_adder_12_c_2));
  full_adder full_adder_13 (.a(in_5[0]), .b(in_5[4]), .c(full_adder_12_c_2), .s(out_6[12]), .c_2(full_adder_13_c_2));
  full_adder full_adder_14 (.a(in_5[1]), .b(in_5[5]), .c(full_adder_13_c_2), .s(out_6[13]), .c_2(full_adder_14_c_2));
  full_adder full_adder_15 (.a(in_5[2]), .b(in_5[6]), .c(full_adder_14_c_2), .s(out_6[14]), .c_2(full_adder_15_c_2));
  full_adder full_adder_16 (.a(in_5[3]), .b(in_5[7]), .c(full_adder_15_c_2), .s(out_6[15]), .c_2(out_7));
endmodule

module _2bit_CLU (
  input  C0,
  input  A0,
  input  B0,
  input  A1,
  input  B1,
  output C1,
  output C2
);

  wire _0_2_out_3, _0_out_3, _1_2_out_3, _1_out_3, and_1_out, and_2_out, and_3_out;

  Propagate _0 (.in_1(A0), .in_2(B0), .out_3(_0_out_3));
  Generate _0_2 (.A(A0), .B(B0), .out_3(_0_2_out_3));
  Propagate _1 (.in_1(A1), .in_2(B1), .out_3(_1_out_3));
  Generate _1_2 (.A(A1), .B(B1), .out_3(_1_2_out_3));
  and and_1 (and_1_out, _0_2_out_3, _1_out_3);
  and and_2 (and_2_out, C0, _0_out_3);
  or or_1 (C1, and_2_out, _0_2_out_3);
  and and_3 (and_3_out, C0, _1_out_3, _0_out_3);
  or or_2 (C2, and_1_out, and_3_out, _1_2_out_3);
endmodule

// G
module Generate (
  input  A,
  input  B,
  output out_3
);

  and and_1 (out_3, A, B);
endmodule

// P
module Propagate (
  input  in_1,
  input  in_2,
  output out_3
);

  xor xor_1 (out_3, in_1, in_2);
endmodule

// S
module Sum (
  input  in_1,
  input  in_2,
  output out_3
);

  xor xor_1 (out_3, in_1, in_2);
endmodule
