// Logisim project register.circ as structural Verilog: 5 circuits, main circuit SR 래치
module \SR_래치  (
  input  in_1,
  input  in_2,
  input  in_3,
  input  in_4,
  output out_5,
  output out_6,
  output out_7,
  output out_8
);

  nand nand_1 (out_5, in_1, out_6);
  nand nand_2 (out_6, out_5, in_2);
  nor nor_1 (out_7, in_3, out_8);
  nor nor_2 (out_8, out_7, in_4);
endmodule

module \게이트_SR_래치  (
  input  in_1,
  input  in_2,
  input  in_3,
  output out_4,
  output out_5
);

  wire and_1_out, and_2_out;

  and and_1 (and_1_out, in_1, in_2);
  and and_2 (and_2_out, in_2, in_3);
  nor nor_1 (out_4, and_1_out, out_5);
  nor nor_2 (out_5, out_4, and_2_out);
endmodule

// D latch
module \게이트_D_latch  (
  input  in_1,
  input  in_2,
  output out_3,
  output out_4
);

  wire and_1_out, and_2_out, not_1_out;

  not not_1 (not_1_out, in_1);
  and and_1 (and_1_out, not_1_out, in_2);
  and and_2 (and_2_out, in_2, in_1);
  nor nor_1 (out_3, and_1_out, out_4);
  nor nor_2 (out_4, out_3, and_2_out);
endmodule

// D FF
module Master_slave_edge_triggered_D_flip_flop (
  input  in_1,
  input  in_2,
  output out_3,
  output out_4
);

  wire not_1_out, \게이트_d_latch_1_out_3 ;

  not not_1 (not_1_out, in_2);
  \게이트_D_latch  \u_게이트_d_latch_1  (.in_1(in_1), .in_2(not_1_out), .out_3(\게이트_d_latch_1_out_3 ));  // open: out_4
  \게이트_D_latch  \u_게이트_d_latch_2  (.in_1(\게이트_d_latch_1_out_3 ), .in_2(in_2), .out_3(out_3), .out_4(out_4));
endmodule

module _4bit_register (
  input  [3:0] in_1,
  input  in_2,
  output [3:0] out_3
);

  Master_slave_edge_triggered_D_flip_flop master_slave_edge_triggered_d_flip_flop_1 (
    .in_1(in_1[0]), .in_2(in_2), .out_3(out_3[0]));  // open: out_4
  Master_slave_edge_triggered_D_flip_flop master_slave_edge_triggered_d_flip_flop_2 (
    .in_1(in_1[1]), .in_2(in_2), .out_3(out_3[1]));  // open: out_4
  Master_slave_edge_triggered_D_flip_flop master_slave_edge_triggered_d_flip_flop_3 (
    .in_1(in_1[2]), .in_2(in_2), .out_3(out_3[2]));  // open: out_4
  Master_slave_edge_triggered_D_flip_flop master_slave_edge_triggered_d_flip_flop_4 (
    .in_1(in_1[3]), .in_2(in_2), .out_3(out_3[3]));  // open: out_4
endmodule
